// Logisim project cpu.circ as structural Verilog: 9 circuits, main circuit main
module main (
  input  [15:0] INSTRUCTION,
  input  in_2,
  output [15:0] FETCH_ADDRESS,
  output [15:0] L_s0_Value_7c9fba82,
  output [15:0] L_s1_Value_2cb75696,
  output [15:0] L_s2_Value_be7b1681,
  output [15:0] L_ra_Value_55886cf9,
  output [15:0] L_sp_Value_a0856b3d,
  output [15:0] L_HI_Value_3bde5b98,
  output [15:0] L_LO_Value_b62659ce
);

  wire and_1_out, and_2_out, branch, controlador_1_out_6, controlador_1_out_9, controlador_1_out_11,
       controlador_1_out_12, controlador_1_out_13, main_2_equal, multiplexer_8_out, not_1_out, or_1_out,
       or_2_out, or_3_out, pulou, pulouj;
  wire [1:0] controlador_1_out_3, controlador_1_out_10, JUMP;
  wire [2:0] aluctl_1_out_3, controlador_1_out_7, funct_1_out_2, multiplexer_3_out, multiplexer_4_out,
       separador_1_out_4, separador_1_out_5, separador_1_out_6, shifter_1_out;
  wire [3:0] controlador_1_out_8, separador_1_out_7;
  wire [5:0] separador_1_out_3;
  wire [9:0] separador_1_out_2;
  wire [15:0] adder_1_out, adder_2_out, adder_3_out, adder_4_out, adder_5_out, bit_extender_1_out,
       bit_extender_2_out, bit_extender_3_out, if_ex_1_out_4, if_ex_1_out_5, main_1_read_data_1_c47ea0d8,
       main_1_read_data_2_34b29906, main_2_result, main_2_result_2_a9898de3, MEM_p5, multiplexer_1_out,
       multiplexer_2_out, multiplexer_5_out, multiplexer_6_out, multiplexer_7_out, multiplexer_9_out,
       multiplexer_10_out, pc_imm_1_out_3;

  Multiplexer #(.width(16), .enable("false")) multiplexer_1 (
    .in0(adder_1_out), .in1(multiplexer_9_out), .out(multiplexer_1_out), .sel(or_1_out));
  or or_1 (or_1_out, pulouj, branch);
  xor xor_1 (pulouj, JUMP[0], JUMP[1]);
  Register #(.width(16)) L_PC_bd1e00e6 (.D(multiplexer_1_out), .clk(in_2), .Q(FETCH_ADDRESS));  // open: en, clr
  Adder #(.width(16)) adder_1 (.a(FETCH_ADDRESS), .b(16'h2), .out(adder_1_out));  // open: cin, cout
  IF_EX if_ex_1 (.in_2(INSTRUCTION), .out_5(if_ex_1_out_5), .in_1(FETCH_ADDRESS), .out_4(if_ex_1_out_4), .in_3(in_2));
  Multiplexer #(.width(16), .enable("false")) multiplexer_2 (
    .in0(if_ex_1_out_5), .in1({16{1'b0}}), .out(multiplexer_2_out), .sel(pulou));
  Separador separador_1 (
    .out_5(separador_1_out_5), .out_4(separador_1_out_4), .out_7(separador_1_out_7),
    .in_1(multiplexer_2_out), .out_6(separador_1_out_6), .out_3(separador_1_out_3), .out_2(separador_1_out_2));
  Controlador controlador_1 (
    .out_5(branch), .out_10(controlador_1_out_10), .out_9(controlador_1_out_9), .in_1(separador_1_out_7),
    .out_6(controlador_1_out_6), .out_7(controlador_1_out_7), .out_8(controlador_1_out_8),
    .out_12(controlador_1_out_12), .in_2(funct_1_out_2), .out_3(controlador_1_out_3), .out_4(JUMP),
    .out_13(controlador_1_out_13), .out_11(controlador_1_out_11));
  Shifter #(.width(3), .shift("lr")) shifter_1 (.in(separador_1_out_6), .\dist (2'b01), .out(shifter_1_out));
  Multiplexer #(.width(3), .enable("false")) multiplexer_3 (
    .in0(separador_1_out_4), .in1(separador_1_out_6), .out(multiplexer_3_out), .sel(or_2_out));
  Multiplexer #(.select(2), .width(3), .enable("false")) multiplexer_4 (
    .in0(separador_1_out_6), .in1(shifter_1_out), .out(multiplexer_4_out), .sel(controlador_1_out_3));  // open: in2, in3
  assign bit_extender_1_out = {{6{1'b0}}, separador_1_out_2};  // Bit_Extender bit_extender_1
  or or_2 (or_2_out, branch, controlador_1_out_9);
  PC_Imm pc_imm_1 (.out_3(pc_imm_1_out_3), .in_1(if_ex_1_out_5), .in_2(if_ex_1_out_4));
  regfile_main main_1 (
    .Read_Register_1_eca808b4(separador_1_out_5), .Read_Register_2_4b336a3e(multiplexer_3_out),
    .Write_Register_1c78e1ef(multiplexer_4_out), .Write_Data_00073c80(multiplexer_10_out),
    .Write_Enable_5f560963(controlador_1_out_11), .Clock(in_2),
    .Read_Data_1_c47ea0d8(main_1_read_data_1_c47ea0d8), .Read_Data_2_34b29906(main_1_read_data_2_34b29906),
    .L_s0_Value_3e1de553(L_s0_Value_7c9fba82), .L_s1_Value_f16d02bf(L_s1_Value_2cb75696),
    .L_s2_Value_6a9ed51f(L_s2_Value_be7b1681), .L_ra_Value_b804995d(L_ra_Value_55886cf9),
    .L_sp_Value_269f0ffd(L_sp_Value_a0856b3d));
  assign bit_extender_2_out = {{10{separador_1_out_3[5]}}, separador_1_out_3};  // Bit_Extender bit_extender_2
  assign bit_extender_3_out = {{10{1'b0}}, separador_1_out_3};  // Bit_Extender bit_extender_3
  funct funct_1 (.in_1(separador_1_out_3), .out_2(funct_1_out_2));
  Multiplexer #(.width(16), .enable("false")) multiplexer_5 (
    .in0(main_1_read_data_1_c47ea0d8), .in1(bit_extender_1_out), .out(multiplexer_5_out),
    .sel(controlador_1_out_13));
  Multiplexer #(.select(2), .width(16), .enable("false")) multiplexer_6 (
    .in0(main_1_read_data_2_34b29906), .in1(bit_extender_2_out), .in2(16'h6), .in3(bit_extender_3_out),
    .out(multiplexer_6_out), .sel(controlador_1_out_10));
  Adder #(.width(16)) adder_2 (.a(if_ex_1_out_4), .b(bit_extender_2_out), .out(adder_2_out));  // open: cin, cout
  not not_1 (not_1_out, main_2_equal);
  alu_main main_2 (
    .Switch(aluctl_1_out_3), .X(multiplexer_5_out), .Equal(main_2_equal), .Result(main_2_result),
    .Y(multiplexer_6_out), .Result_2_a9898de3(main_2_result_2_a9898de3));
  ALUctl aluctl_1 (.out_3(aluctl_1_out_3), .in_2(controlador_1_out_8), .in_1(funct_1_out_2));
  Adder #(.width(16)) adder_3 (.a(if_ex_1_out_4), .b(16'h4), .out(adder_3_out));  // open: cin, cout
  and and_1 (and_1_out, branch, main_2_equal);
  and and_2 (and_2_out, branch, not_1_out);
  Multiplexer #(.width(16), .enable("false")) multiplexer_7 (
    .in0(adder_3_out), .in1(adder_2_out), .out(multiplexer_7_out), .sel(multiplexer_8_out));
  Adder #(.width(16)) adder_4 (
    .a(bit_extender_2_out), .b(main_1_read_data_1_c47ea0d8), .out(adder_4_out));  // open: cin, cout
  Multiplexer #(.enable("false")) multiplexer_8 (
    .in0(and_1_out), .in1(and_2_out), .out(multiplexer_8_out), .sel(controlador_1_out_6));
  Register #(.width(16)) L_LO_ba622f5d (
    .D(main_2_result), .en(controlador_1_out_12), .clk(in_2), .Q(L_LO_Value_b62659ce));  // open: clr
  Register #(.width(16)) L_HI_1d3f3066 (
    .D(main_2_result_2_a9898de3), .en(controlador_1_out_12), .clk(in_2), .Q(L_HI_Value_3bde5b98));  // open: clr
  Multiplexer #(.select(2), .width(16), .enable("false")) multiplexer_9 (
    .in0(multiplexer_7_out), .in1(pc_imm_1_out_3), .in2(adder_4_out), .out(multiplexer_9_out), .sel(JUMP));  // open: in3
  or or_3 (or_3_out, pulouj, multiplexer_8_out);
  Adder #(.width(16)) adder_5 (.a(16'h2), .b(if_ex_1_out_4), .out(adder_5_out));  // open: cin, cout
  // mem_main MEM: pin names not known; wires that end beside it: main_2_result, main_1_read_data_2_34b29906, controlador_1_out_9, in_2, MEM_p5, in_2
  Register #(.width(1)) register_1 (.D(or_3_out), .clk(in_2), .Q(pulou));  // open: en, clr
  Multiplexer #(.select(3), .width(16), .enable("false")) multiplexer_10 (
    .in0(main_2_result), .in1(MEM_p5), .in2(adder_5_out), .in3(L_HI_Value_3bde5b98),
    .in4(L_LO_Value_b62659ce), .out(multiplexer_10_out), .sel(controlador_1_out_7));  // open: in5, in6, in7

  // Other names for the same wires on the sheet: clk = in_2; fetch_addr[15:0] = FETCH_ADDRESS;
  //   HI[15:0] = L_HI_Value_3bde5b98; LO[15:0] = L_LO_Value_b62659ce; ra[15:0] = L_ra_Value_55886cf9;
  //   s0[15:0] = L_s0_Value_7c9fba82; s1[15:0] = L_s1_Value_2cb75696; s2[15:0] = L_s2_Value_be7b1681;
  //   sp[15:0] = L_sp_Value_a0856b3d

  // Notes on the sheet:
  //   Output
  //   These are outputs/inputs from run.circ
  //   Inputs
  //   These are DEBUG/TEST outputs from your circuit.
endmodule

module Separador (
  input  [15:0] in_1,
  output [9:0] out_2,
  output [5:0] out_3,
  output [2:0] out_4,
  output [2:0] out_5,
  output [2:0] out_6,
  output [3:0] out_7
);


  assign out_2 = in_1[9:0];
  assign out_3 = in_1[5:0];
  assign out_4 = in_1[5:3];
  assign out_5 = in_1[8:6];
  assign out_6 = in_1[11:9];
  assign out_7 = in_1[15:12];
endmodule

module IF_EX (
  input  [15:0] in_1,
  input  [15:0] in_2,
  input  in_3,
  output [15:0] out_4,
  output [15:0] out_5
);

  Register #(.width(16)) register_1 (.D(in_1), .clk(in_3), .Q(out_4));  // open: en, clr
  Register #(.width(16)) register_2 (.D(in_2), .clk(in_3), .Q(out_5));  // open: en, clr
endmodule

module Controlador (
  input  [3:0] in_1,
  input  [2:0] in_2,
  output [1:0] out_3,
  output [1:0] out_4,
  output out_5,
  output out_6,
  output [2:0] out_7,
  output [3:0] out_8,
  output out_9,
  output [1:0] out_10,
  output out_11,
  output out_12,
  output out_13
);

  wire multiplexer_1_out, multiplexer_2_out;
  wire [1:0] conv1to2_1_out_2, conv1to2_2_out_2, conv1to2_3_out_2, conv1to2_4_out_2, conv1to2_5_out_2,
       conv1to2_6_out_2;
  wire [2:0] c1to3_1_out_2, c1to3_2_out_2;
  wire [3:1] and_1_out;

  conv1to2 conv1to2_1 (.out_2(conv1to2_1_out_2), .in_1(1'b0));
  conv1to2 conv1to2_2 (.out_2(conv1to2_2_out_2), .in_1(1'b0));
  c1to3 c1to3_1 (.out_2(c1to3_1_out_2), .in_1(1'b0));
  conv1to2 conv1to2_3 (.out_2(conv1to2_3_out_2), .in_1(1'b0));
  conv1to2 conv1to2_4 (.out_2(conv1to2_4_out_2), .in_1(1'b1));
  conv1to2 conv1to2_5 (.out_2(conv1to2_5_out_2), .in_1(1'b1));
  c1to3 c1to3_2 (.out_2(c1to3_2_out_2), .in_1(1'b1));
  conv1to2 conv1to2_6 (.out_2(conv1to2_6_out_2), .in_1(1'b1));
  Comparator #(.width(4)) comparator_1 (.a(in_1), .b(4'b0001), .eq(out_13));  // open: gt, lt
  Multiplexer #(.select(3), .enable("false")) multiplexer_1 (
    .in0(1'b1), .in1(1'b1), .in2(1'b1), .in3(1'b1), .in4(1'b1), .in5(1'b1), .in6(1'b1), .in7(1'b0),
    .out(multiplexer_1_out), .sel(in_2));
  Multiplexer #(.select(3), .enable("false")) multiplexer_2 (
    .in0(1'b0), .in1(1'b0), .in2(1'b0), .in3(1'b0), .in4(1'b0), .in5(1'b0), .in6(1'b0), .in7(1'b1),
    .out(multiplexer_2_out), .sel(in_2));
  Multiplexer #(.select(4), .width(2), .enable("false")) multiplexer_3 (
    .in0(conv1to2_1_out_2), .in1(conv1to2_4_out_2), .in2(conv1to2_4_out_2), .in3(conv1to2_1_out_2),
    .in4(conv1to2_1_out_2), .in5(conv1to2_1_out_2), .in6(conv1to2_1_out_2), .in7(conv1to2_1_out_2),
    .in8(conv1to2_1_out_2), .in9(conv1to2_1_out_2), .in10(conv1to2_1_out_2), .in11(conv1to2_1_out_2),
    .in12(conv1to2_1_out_2), .in13(conv1to2_1_out_2), .in14(conv1to2_1_out_2), .in15(conv1to2_1_out_2),
    .out(out_3), .sel(in_1));
  Multiplexer #(.select(4), .width(2), .enable("false")) multiplexer_4 (
    .in0(conv1to2_2_out_2), .in1(conv1to2_2_out_2), .in2(conv1to2_5_out_2), .in3(2'b10),
    .in4(conv1to2_2_out_2), .in5(conv1to2_2_out_2), .in6(conv1to2_2_out_2), .in7(conv1to2_2_out_2),
    .in8(conv1to2_2_out_2), .in9(conv1to2_2_out_2), .in10(conv1to2_2_out_2), .in11(conv1to2_2_out_2),
    .in12(conv1to2_2_out_2), .in13(conv1to2_2_out_2), .in14(conv1to2_2_out_2), .in15(conv1to2_2_out_2),
    .out(out_4), .sel(in_1));
  Multiplexer #(.select(4), .enable("false")) multiplexer_5 (
    .in0(1'b0), .in1(1'b0), .in2(1'b0), .in3(1'b0), .in4(1'b1), .in5(1'b1), .in6(1'b0), .in7(1'b0),
    .in8(1'b0), .in9(1'b0), .in10(1'b0), .in11(1'b0), .in12(1'b0), .in13(1'b0), .in14(1'b0), .in15(1'b0),
    .out(out_5), .sel(in_1));
  assign {and_1_out, out_6} = 4'b0001 & in_1;  // AND_Gate and_1, 4 bits wide
  Multiplexer #(.select(4), .width(3), .enable("false")) multiplexer_6 (
    .in0(c1to3_1_out_2), .in1(c1to3_1_out_2), .in2(3'b010), .in3(3'b010), .in4(c1to3_1_out_2),
    .in5(c1to3_1_out_2), .in6(c1to3_1_out_2), .in7(c1to3_1_out_2), .in8(c1to3_1_out_2), .in9(c1to3_1_out_2),
    .in10(c1to3_2_out_2), .in11(c1to3_2_out_2), .in12(3'b011), .in13(3'b100), .out(out_7), .sel(in_1));  // open: in14, in15
  Multiplexer #(.select(4), .enable("false")) multiplexer_7 (
    .in0(1'b0), .in1(1'b0), .in2(1'b0), .in3(1'b0), .in4(1'b0), .in5(1'b0), .in6(1'b0), .in7(1'b0),
    .in8(1'b0), .in9(1'b0), .in10(1'b0), .in11(1'b1), .in12(1'b0), .in13(1'b0), .out(out_9), .sel(in_1));  // open: in14, in15
  Multiplexer #(.select(4), .width(2), .enable("false")) multiplexer_8 (
    .in0(conv1to2_3_out_2), .in1(2'b10), .in2(conv1to2_6_out_2), .in3(conv1to2_6_out_2),
    .in4(conv1to2_3_out_2), .in5(conv1to2_3_out_2), .in6(conv1to2_6_out_2), .in7(conv1to2_6_out_2),
    .in8(2'b11), .in9(2'b11), .in10(conv1to2_6_out_2), .in11(conv1to2_6_out_2), .in12(conv1to2_3_out_2),
    .in13(conv1to2_3_out_2), .out(out_10), .sel(in_1));  // open: in14, in15
  Multiplexer #(.select(4), .enable("false")) multiplexer_9 (
    .in0(multiplexer_1_out), .in1(1'b0), .in2(1'b1), .in3(1'b1), .in4(1'b0), .in5(1'b0), .in6(1'b1),
    .in7(1'b1), .in8(1'b1), .in9(1'b1), .in10(1'b1), .in11(1'b0), .in12(1'b1), .in13(1'b1), .out(out_11),
    .sel(in_1));  // open: in14, in15
  Multiplexer #(.select(4), .enable("false")) multiplexer_10 (
    .in0(multiplexer_2_out), .in1(1'b1), .in2(1'b0), .in3(1'b0), .in4(1'b0), .in5(1'b0), .in6(1'b0),
    .in7(1'b0), .in8(1'b0), .in9(1'b0), .in10(1'b0), .in11(1'b0), .in12(1'b0), .in13(1'b0), .in14(1'b0),
    .in15(1'b0), .out(out_12), .sel(in_1));

  assign out_8 = in_1;

  // Other names for the same wires on the sheet: whichBranch = out_6; ALUSrc[1:0] = out_10; Branch = out_5;
  //   funct[2:0] = in_2; isLU = out_13; Jump[1:0] = out_4; MemtoReg[2:0] = out_7; MemWrite = out_9; ALUOp[3:0] = in_1;
  //   opcode[3:0] = in_1; RegDst[1:0] = out_3; RegWrite = out_11; WriteLO = out_12
endmodule

module conv1to2 (
  input  in_1,
  output [1:0] out_2
);

  Multiplexer #(.width(2), .enable("false")) multiplexer_1 (.in0(2'b00), .in1(2'b01), .out(out_2), .sel(in_1));
endmodule

module funct (
  input  [5:0] in_1,
  output [2:0] out_2
);


  assign out_2 = in_1[2:0];
endmodule

module ALUctl (
  input  [2:0] in_1,
  input  [3:0] in_2,
  output [2:0] out_3
);

  wire [2:0] multiplexer_1_out;

  Multiplexer #(.select(3), .width(3), .enable("false")) multiplexer_1 (
    .in0(3'b000), .in1(3'b001), .in2(3'b010), .in3(3'b011), .in4(3'b100), .in5(3'b101), .in6(3'b110),
    .in7(3'b111), .out(multiplexer_1_out), .sel(in_1));
  Multiplexer #(.select(4), .width(3), .enable("false")) multiplexer_2 (
    .in0(multiplexer_1_out), .in1(3'b000), .in2(3'b010), .in3(3'b010), .in4(3'b010), .in5(3'b010),
    .in6(3'b010), .in7(3'b110), .in8(3'b011), .in9(3'b100), .in10(3'b010), .in11(3'b010), .out(out_3),
    .sel(in_2));  // open: in12, in13, in14, in15
endmodule

module PC_Imm (
  input  [15:0] in_1,
  input  [15:0] in_2,
  output [15:0] out_3
);


  assign out_3 = {in_2[15:10], in_1[9:0]};
endmodule

module c1to3 (
  input  in_1,
  output [2:0] out_2
);


  assign out_2 = {2'b00, in_1};
endmodule
