// Logisim project run.circ as structural Verilog: 1 circuit, main circuit main
module main (
  output [15:0] s0_Value,
  output [15:0] s1_Value,
  output [15:0] s2_Value,
  output [15:0] ra_Value,
  output [15:0] sp_Value,
  output [15:0] hi_Value,
  output [15:0] lo_Value,
  output [15:0] Time_Step,
  output [15:0] Requested_Address,
  output [15:0] Requested_Instruction
);

  wire clock_1_out;

  Clock clock_1 (.out(clock_1_out));
  Counter #(.width(16), .max('hffff)) counter_1 (
    .clk(clock_1_out), .Q(Time_Step));  // open: clr, load, up, count, D, carry
  cpu_main main_1 (
    .INSTRUCTION(Requested_Instruction), .in_2(clock_1_out), .FETCH_ADDRESS(Requested_Address),
    .L_s0_Value_7c9fba82(s0_Value), .L_s1_Value_2cb75696(s1_Value), .L_s2_Value_be7b1681(s2_Value),
    .L_ra_Value_55886cf9(ra_Value), .L_LO_Value_b62659ce(lo_Value), .L_HI_Value_3bde5b98(hi_Value),
    .L_sp_Value_a0856b3d(sp_Value));
  // Probe on Requested_Address
  ROM #(.addrWidth(14), .dataWidth(16)) rom_1 (.addr(Requested_Address[14:1]), .data(Requested_Instruction));
  // Probe on Requested_Instruction

  // Other names for the same wires on the sheet: fetch_addr[15:0] = Requested_Address;
  //   Instruction[15:0] = Requested_Instruction

  // Notes on the sheet:
  //   YOUR CPU SHOULD FIT IN HERE!
  //   contents of rom_1 (hex, n*v repeats v):
  //   6900 6d8a 4dd4 6fc1 68c3 951f 4a4 6a3 88ff 530 4b1 2004 66f7 5d8 95f7 9882
  //   Instruction Memory
endmodule
