// Logisim project regfile.circ as structural Verilog: 2 circuits, main circuit main
module main (
  input  [2:0] Read_Register_1_eca808b4,
  input  [2:0] Read_Register_2_4b336a3e,
  input  [2:0] Write_Register_1c78e1ef,
  input  [15:0] Write_Data_00073c80,
  input  Write_Enable_5f560963,
  input  Clock,
  output [15:0] L_s0_Value_3e1de553,
  output [15:0] L_s1_Value_f16d02bf,
  output [15:0] L_s2_Value_6a9ed51f,
  output [15:0] L_ra_Value_b804995d,
  output [15:0] L_sp_Value_269f0ffd,
  output [15:0] Read_Data_1_c47ea0d8,
  output [15:0] Read_Data_2_34b29906
);

  Registers registers_1 (
    .Write_register(Write_Register_1c78e1ef), .in_1(Clock), .out_12(Read_Data_1_c47ea0d8),
    .Read_B(Read_Register_2_4b336a3e), .Write_Enable(Write_Enable_5f560963),
    .Read_A(Read_Register_1_eca808b4), .in_2(Write_Data_00073c80), .out_13(Read_Data_2_34b29906),
    .out_7(L_s0_Value_3e1de553), .out_9(L_s2_Value_6a9ed51f), .out_8(L_s1_Value_f16d02bf),
    .out_10(L_ra_Value_b804995d), .out_11(L_sp_Value_269f0ffd));

  // Other names for the same wires on the sheet: clk = Clock; read_data1[15:0] = Read_Data_1_c47ea0d8;
  //   read_data2[15:0] = Read_Data_2_34b29906; read_reg1[2:0] = Read_Register_1_eca808b4;
  //   read_reg2[2:0] = Read_Register_2_4b336a3e; write_data[15:0] = Write_Data_00073c80;
  //   write_en = Write_Enable_5f560963; write_reg[2:0] = Write_Register_1c78e1ef

  // Notes on the sheet:
  //   INPUTS to your circuit
  //   DON'T CHANGE THE LOCATIONS OF THE INPUTS AND OUTPUTS!
  //   These are DEBUG/TEST outputs from your circuit.
  //   OUTPUTS from your circuit
endmodule

module Registers (
  input  in_1,
  input  [15:0] in_2,
  input  [2:0] Read_A,
  input  Write_Enable,
  input  [2:0] Write_register,
  input  [2:0] Read_B,
  output [15:0] out_7,
  output [15:0] out_8,
  output [15:0] out_9,
  output [15:0] out_10,
  output [15:0] out_11,
  output [15:0] out_12,
  output [15:0] out_13
);

  wire demultiplexer_1_out0, demultiplexer_1_out1, demultiplexer_1_out2, demultiplexer_1_out3,
       demultiplexer_1_out4, demultiplexer_1_out5, demultiplexer_1_out6, demultiplexer_1_out7;
  wire [15:0] register_1_q, register_6_q, register_7_q;

  Demultiplexer #(.select(3), .enable("false")) demultiplexer_1 (
    .out0(demultiplexer_1_out0), .out1(demultiplexer_1_out1), .out2(demultiplexer_1_out2),
    .out3(demultiplexer_1_out3), .out4(demultiplexer_1_out4), .out5(demultiplexer_1_out5),
    .out6(demultiplexer_1_out6), .out7(demultiplexer_1_out7), .in(Write_Enable), .sel(Write_register));
  Register #(.width(16)) register_1 (.D(in_2), .en(demultiplexer_1_out0), .clk(in_1), .Q(register_1_q), .clr(1'b1));
  Register #(.width(16)) register_2 (.D(in_2), .en(demultiplexer_1_out1), .clk(in_1), .Q(out_10));  // open: clr
  Register #(.width(16)) register_3 (.D(in_2), .en(demultiplexer_1_out2), .clk(in_1), .Q(out_7));  // open: clr
  Register #(.width(16)) register_4 (.D(in_2), .en(demultiplexer_1_out3), .clk(in_1), .Q(out_8));  // open: clr
  Register #(.width(16)) register_5 (.D(in_2), .en(demultiplexer_1_out4), .clk(in_1), .Q(out_9));  // open: clr
  Register #(.width(16)) register_6 (.D(in_2), .en(demultiplexer_1_out5), .clk(in_1), .Q(register_6_q));  // open: clr
  Register #(.width(16)) register_7 (.D(in_2), .en(demultiplexer_1_out6), .clk(in_1), .Q(register_7_q));  // open: clr
  Register #(.width(16)) register_8 (.D(in_2), .en(demultiplexer_1_out7), .clk(in_1), .Q(out_11));  // open: clr
  Multiplexer #(.select(3), .width(16), .enable("false")) multiplexer_1 (
    .in0(register_1_q), .in1(out_10), .in2(out_7), .in3(out_8), .in4(out_9), .in5(register_6_q),
    .in6(register_7_q), .in7(out_11), .out(out_12), .sel(Read_A));
  Multiplexer #(.select(3), .width(16), .enable("false")) multiplexer_2 (
    .in0(register_1_q), .in1(out_10), .in2(out_7), .in3(out_8), .in4(out_9), .in5(register_6_q),
    .in6(register_7_q), .in7(out_11), .out(out_13), .sel(Read_B));
endmodule
