// Logisim project alu.circ as structural Verilog: 4 circuits, main circuit main
module main (
  input  [15:0] X,
  input  [15:0] Y,
  input  [2:0] Switch,
  output Equal,
  output [15:0] Result,
  output [15:0] Result_2_a9898de3
);

  ALU alu_1 (.in_1(X), .in_2(Y), .in_3(Switch), .out_4(Equal), .out_5(Result), .out_6(Result_2_a9898de3));

  // Other names for the same wires on the sheet: result_2[15:0] = Result_2_a9898de3; S[2:0] = Switch

  // Notes on the sheet:
  //   INPUTS to your circuit
  //   DON'T CHANGE THE LOCATIONS OF THE INPUTS AND OUTPUTS!
  //   OUTPUTS from your circuit
endmodule

module ALU (
  input  [15:0] in_1,
  input  [15:0] in_2,
  input  [2:0] in_3,
  output out_4,
  output [15:0] out_5,
  output [15:0] out_6
);

  wire comparator_1_lt;
  wire [3:0] conv4_1_out_2, conv4_2_out_2;
  wire [15:0] adder_1_out, and_1_out, conv16_1_out_2, multiplier_1_out, or_1_out, shifter_1_out,
       shifter_2_out, xor_1_out;

  conv4 conv4_1 (.in_1(in_2), .out_2(conv4_1_out_2));
  conv4 conv4_2 (.in_1(in_2), .out_2(conv4_2_out_2));
  assign and_1_out = in_1 & in_2;  // AND_Gate and_1, 16 bits wide
  Shifter #(.width(16)) shifter_1 (.in(in_1), .\dist (conv4_1_out_2), .out(shifter_1_out));
  assign or_1_out = in_1 | in_2;  // OR_Gate or_1, 16 bits wide
  assign xor_1_out = in_1 ^ in_2;  // XOR_Gate xor_1, 16 bits wide
  Shifter #(.width(16), .shift("lr")) shifter_2 (.in(in_1), .\dist (conv4_2_out_2), .out(shifter_2_out));
  Multiplier #(.width(16)) multiplier_1 (.a(in_1), .b(in_2), .out(multiplier_1_out), .cout(out_6));  // open: cin
  Adder #(.width(16)) adder_1 (.a(in_1), .b(in_2), .out(adder_1_out));  // open: cin, cout
  Comparator #(.width(16)) comparator_1 (.a(in_1), .b(in_2), .lt(comparator_1_lt));  // open: gt, eq
  Comparator #(.width(16)) comparator_2 (.a(in_1), .b(in_2), .eq(out_4));  // open: gt, lt
  conv16 conv16_1 (.out_2(conv16_1_out_2), .in_1(comparator_1_lt));
  Multiplexer #(.select(3), .width(16), .enable("false")) multiplexer_1 (
    .in0(shifter_1_out), .in1(shifter_2_out), .in2(adder_1_out), .in3(and_1_out), .in4(or_1_out),
    .in5(xor_1_out), .in6(conv16_1_out_2), .in7(multiplier_1_out), .out(out_5), .sel(in_3));
endmodule

module conv16 (
  input  in_1,
  output [15:0] out_2
);


  assign out_2 = {{15{1'b0}}, in_1};
endmodule

module conv4 (
  input  [15:0] in_1,
  output [3:0] out_2
);


  assign out_2 = in_1[3:0];
endmodule
